// Logisim project 8-bit TTL Cpu.circ as structural Verilog: 1 circuit, main circuit main
module main (
);

  wire and_1_out, CLK_B, clock_1_out, decoder_1_out5, Execute, Fetch_1, Fetch_2, Fetch_3, Fetch_4;
  wire [2:0] counter_1_q;
  wire [7:0] ram_1_data;
  wire [15:0] PC_q;

  Clock clock_1 (.out(clock_1_out));
  Counter #(.width(3), .max('h7)) counter_1 (
    .count(1'b1), .Q(counter_1_q), .clk(clock_1_out), .clr(decoder_1_out5));  // open: load, D, carry
  Decoder #(.select(3)) decoder_1 (
    .out0(Fetch_1), .out1(Fetch_2), .out2(Fetch_3), .out3(Fetch_4), .out4(Execute), .out5(decoder_1_out5),
    .sel(counter_1_q));  // open: out6, out7, en
  not not_1 (CLK_B, clock_1_out);
  Register #(.width(16)) PC (.Q(PC_q));  // open: D, en, clk, clr
  RAM #(.addrWidth(16)) ram_1 (.addr(PC_q), .data(ram_1_data));  // open: sel, clk, ld, clr
  and and_1 (and_1_out, Fetch_1, CLK_B);
  Register IR_0 (.D(ram_1_data), .clk(and_1_out));  // open: en, Q, clr
  Register IR_1 (.D(ram_1_data));  // open: en, Q, clk, clr
  Register IR_2 (.D(ram_1_data));  // open: en, Q, clk, clr
  Register IR_3 (.D(ram_1_data));  // open: en, Q, clk, clr

  // Notes on the sheet:
  //   Equiv to 74HCT4017
  //   Least significant byte
endmodule
